# Fritzing sketch GloveHero (saved by Fritzing 0.9.9b)
breadboards: 1

parts:
  MP3-1 = Serial MP3 Player
  Pinky = Round Pushbutton
  Index_Finger = Round Pushbutton
  Middle_Finger = Round Pushbutton
  Ring_Finger = Round Pushbutton
  BAT1 = Battery Holders [package=battery-aaa]
  BAT2 = Battery Holders [package=battery-aaa]
  BAT3 = Battery Holders [package=battery-aaa]
  ESP32 = ESP32S-DevKit [part_number=ESP32S-DevKit]
  NEOPIXEL1 = Neopixel Strip -- Black (30/m)
  S1 = SWITCH-DPDT [package=gpi-152-3013]

nets:
  GND: MP3-1.pin1, Pinky.leg1, Index_Finger.leg1, Middle_Finger.leg1, Ring_Finger.leg1, BAT1.-, ESP32.GND, NEOPIXEL1.GND
  VIN: MP3-1.pin2, ESP32.VIN, NEOPIXEL1.+5V, S1.1
  N1: MP3-1.pin3, ESP32.GPIO19
  N2: MP3-1.pin4, ESP32.GPIO35
  N3: Pinky.leg0, ESP32.GPIO27
  N4: Index_Finger.leg0, ESP32.GPIO13
  N5: Middle_Finger.leg0, ESP32.GPIO12
  N6: Ring_Finger.leg0, ESP32.GPIO14
  N7: BAT1.+, BAT2.-
  N8: BAT2.+, BAT3.-
  N9: BAT3.+, S1.2
  N10: ESP32.GPIO26, NEOPIXEL1.DI

notes:
  Thumb

custom parts:
  Serial MP3 Player: The module is a kind of simple MP3 player device which is based on a high-quality MP3 audio chip---YX5300. It can support 8k Hz ~ 48k Hz sampling frequency MP3 and WAV file formats. There is a TF card socket on board, so you can plug the micro SD card that stores audio files. MCU can control the MP3 playback state by sending commands to the module via UART port, such as switch songs, change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
  Neopixel Strip -- Black (30/m): Neopixel Strip, Black, 30 pixels per meter.
